# Fritzing sketch Volt_Eimer (saved by Fritzing 0.9.3b)
circuit board: 8.46667cm x 5.64444cm

parts:
  Bauteil1 = Arduino Micro (Rev3)
  LED1 = RGB LED - (4 legs) [package="5 mm [THT]"]
  R1 = Resistor [tolerance=±5% resistance=1k package=THT]
  LED2 = RGB LED - (4 legs) [package="5 mm [THT]"]
  R3 = Resistor [tolerance=±5% resistance=100k package=THT]

nets:
  N1: Bauteil1.GND, R3.Pin_0
  N2: Bauteil1.D3/SCL, R1.Pin_1
  N3: Bauteil1.5V, LED1.common_anode, LED2.common_anode
  N4: Bauteil1.A5, LED1.red_cathode
  N5: Bauteil1.A3, R3.Pin_1
  N6: LED1.blue_cathode, LED2.red_cathode

notes:
  EIMER
